# Fritzing sketch schema (saved by Fritzing 1.0.0d)

parts:
  Компонент1 = Arduino Nano (Rev3.0) (ICSP)
  S1 = Pushbutton [package="[SMD]"]
  S2 = Pushbutton [package="[SMD]"]
  S3 = Pushbutton [package="[SMD]"]
  S4 = Pushbutton [package="[SMD]"]
  LCD2 = LCD screen
  LCM1602_IIC2 = LCM1602 IIC [part_number="LCM1602 IIC" chip_label="LCM1602 IIC" package="DIP (Dual Inline) [THT]"]
  RTC1 = DS3231 AT24C32 Real Time Clock
  DS1 = DS18B20 1-Wire Temperature Sensor [part_number=DS18B20]
  DS2 = DS18B20 1-Wire Temperature Sensor [part_number=DS18B20]
  R1 = Resistor [tolerance=±5% power=0.25W resistance=220 package=THT]  # not connected
  R2 = Resistor [tolerance=±5% power=0.25W resistance=220 package=THT]  # not connected

nets:
  GND: Компонент1.GND, DS1.GND
  N1: Компонент1.D2, DS1.DQ
  N2: Компонент1.D3, DS2.DQ
  N3: Компонент1.D5, S4.Pin_4
  N4: Компонент1.D6, S3.Pin_4
  N5: Компонент1.D7, S2.Pin_4
  N6: Компонент1.D8, S1.Pin_4
  N7: Компонент1.D9, DS2.VDD
  N8: Компонент1.D10, RTC1.VCC
  N9: Компонент1.D11/MOSI, LCM1602_IIC2.VCC
  N10: Компонент1.A5, LCM1602_IIC2.SCL
  N11: Компонент1.A4, LCM1602_IIC2.SDA
  VSS: LCD2.VSS, LCM1602_IIC2.VSS
  VDD: LCD2.VDD, LCM1602_IIC2.VDD
  N12: LCD2.V0, LCM1602_IIC2.V0
  N13: LCD2.RS, LCM1602_IIC2.RS
  N14: LCD2.R/W, LCM1602_IIC2.RW
  N15: LCD2.E, LCM1602_IIC2.E
  N16: LCD2.DB0, LCM1602_IIC2.D0
  N17: LCD2.DB1, LCM1602_IIC2.D1
  N18: LCD2.DB2, LCM1602_IIC2.D2
  N19: LCD2.DB3, LCM1602_IIC2.D3
  N20: LCD2.DB4, LCM1602_IIC2.D4
  N21: LCD2.DB5, LCM1602_IIC2.D5
  N22: LCD2.DB6, LCM1602_IIC2.D6
  N23: LCD2.DB7, LCM1602_IIC2.D7
  N24: LCD2.LED+, LCM1602_IIC2.A
  N25: LCD2.LED-, LCM1602_IIC2.K
  N26: LCM1602_IIC2.LED_A, LCM1602_IIC2.LED_B

notes:
  4.7kOm

custom parts:
  LCM1602 IIC: I2C-Module to use a 1602 or 2004 LCD on with the wire.h libory Serial LCD Modul
  DS3231 AT24C32 Real Time Clock: Real-time clock basedo on chip DS3231, plus memory chip AT24C32 (32 Kb storage capacity). On-chip temperature sensor with an accuracy of ±3 ℃, I2C bus interface maximum speed: 400 kHz. Operating voltage: 3.3 V to 5.5 V with battery backup capabilities.
